# Fritzing sketch IRrecDump2 (saved by Fritzing 0.9.2b)
breadboards: 1

parts:
  IR1 = TSOP34838 [package=THT]
  Part1 = Arduino Ethernet Shield (Rev3)

nets:
  N1: IR1.Data, Part1.PWM_D11
  GND: IR1.GND, Part1.GND
  N2: IR1.Vs, Part1.5V

custom parts:
  TSOP34838: The TSOP322.., TSOP348.., TSOP324.. and TSOP344.. series are miniaturized IR receiver modules for infrared remote control systems. A PIN diode and a preamplifier are assembled on lead frame, the epoxy package contains an IR filter. The demodulated output signal can be directly connected to a microprocessor for decoding. The TSOP324.., TSOP344.. series devices are optimized to suppress almost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
