# Fritzing sketch Button4 (saved by Fritzing 0.9.2b)
breadboards: 1

parts:
  Part1 = Arduino Ethernet Shield (Rev3)
  S1 = Pushbutton [package="[SMD]"]
  R1 = Resistor [tolerance=±5% resistance=220 package="2512 [SMD]"]
  LED1 = LED - 5mm [color="Infrared (940nm)" package="5 mm [THT]"]
  R2 = Resistor [tolerance=±5% resistance=220 package="2512 [SMD]"]

nets:
  N1: Part1.5V, S1.Pin_3, S1.Pin_4
  N2: Part1.GND, LED1.cathode, R2.Pin_1
  N3: Part1.D2, S1.Pin_1, S1.Pin_2, R2.Pin_0
  N4: Part1.PWM_D3, R1.Pin_1
  N5: R1.Pin_0, LED1.anode
