# Fritzing sketch IRsendRecieveBtn (saved by Fritzing 0.9.2b)
breadboards: 1

parts:
  Part1 = Arduino Ethernet Shield (Rev3)
  S1 = Pushbutton [package="[SMD]"]
  R1 = Resistor [tolerance=±5% resistance=220 package="2512 [SMD]"]
  LED1 = LED - 5mm [color="Infrared (940nm)" package="5 mm [THT]"]
  R2 = Resistor [tolerance=±5% resistance=220 package="2512 [SMD]"]
  IR1 = TSOP34838 [package=THT]

nets:
  N1: Part1.PWM_D11, IR1.Data
  GND: Part1.GND, LED1.cathode, R2.Pin_1, IR1.GND
  N2: Part1.D2, S1.Pin_1, S1.Pin_2, R2.Pin_0
  N3: Part1.PWM_D3, R1.Pin_1
  N4: Part1.5V, S1.Pin_3, S1.Pin_4, IR1.Vs
  N5: R1.Pin_0, LED1.anode

custom parts:
  TSOP34838: The TSOP322.., TSOP348.., TSOP324.. and TSOP344.. series are miniaturized IR receiver modules for infrared remote control systems. A PIN diode and a preamplifier are assembled on lead frame, the epoxy package contains an IR filter. The demodulated output signal can be directly connected to a microprocessor for decoding. The TSOP324.., TSOP344.. series devices are optimized to suppress almost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
