# Fritzing sketch MasterSlave (saved by Fritzing 0.9.2b)
breadboards: 1

parts:
  Part1 = Arduino Nano (Rev3.0)
  Part2 = Arduino Nano (Rev3.0)
  LED2 = LED - 5mm [color="Infrared (940nm)" package="5 mm [THT]"]
  R2 = Resistor [tolerance=±5% resistance=220 package="2512 [SMD]"]
  IR2 = TSOP34838 [package=THT]
  S2 = Pushbutton [package="[SMD]"]
  R3 = Resistor [tolerance=±5% resistance=220 package="2512 [SMD]"]

nets:
  GND: Part1.GND, Part2.GND, LED2.cathode, IR2.GND, S2.Pin_3, S2.Pin_4, R3.Pin_1
  N1: Part1.D2, S2.Pin_1, S2.Pin_2, R3.Pin_0
  N2: Part1.D11/MOSI, IR2.Data
  N3: Part1.5V, IR2.Vs
  N4: Part1.A5, Part2.A5
  N5: Part1.A4, Part2.A4
  N6: Part2.D2, R2.Pin_1
  N7: LED2.anode, R2.Pin_0

custom parts:
  TSOP34838: The TSOP322.., TSOP348.., TSOP324.. and TSOP344.. series are miniaturized IR receiver modules for infrared remote control systems. A PIN diode and a preamplifier are assembled on lead frame, the epoxy package contains an IR filter. The demodulated output signal can be directly connected to a microprocessor for decoding. The TSOP324.., TSOP344.. series devices are optimized to suppress almost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
