# Fritzing sketch Astable555 (saved by Fritzing 0.9.3b)
breadboards: 1

parts:
  U1 = 555 Timer [package="SO8 [SMD]"]  # not connected
  C1 = Electrolytic Capacitor [capacitance=4.7µF voltage=10V package="100 mil [THT, electrolytic]"]
  Part1 = Arduino Nano (Rev3.0) (ICSP)
  C2 = Tantalum Capacitor [capacitance=0.1µF package="100 mil [THT, tantalum]"]
  R2 = Resistor [tolerance=±1% resistance=2.7 package=THT]
  R1 = Resistor [tolerance=±0.1% resistance=2.7 package=THT]
  R3 = Resistor [tolerance=±0.1% resistance=100k package=THT]
  LED1 = smd LED [color="Infrared (940nm)" package="0805 [SMD]"]
  R4 = Resistor [tolerance=±1% resistance=20 package=THT]

nets:
  N1: C1.-, R1.Pin_1
  N2: C1.+, Part1.GND, C2.+, R3.Pin_1, LED1.cathode
  N3: Part1.D2, R3.Pin_0
  N4: Part1.5V, R2.Pin_0
  N5: R2.Pin_1, R1.Pin_0
  N6: LED1.anode, R4.Pin_0
