# Fritzing sketch HeadTag (saved by Fritzing 0.9.2b)
circuit board: 8.46667cm x 5.64444cm
breadboards: 1

parts:
  IR2 = TSOP34838 [package=THT]
  IR3 = TSOP34838 [package=THT]
  Part1 = Arduino Uno (Rev3) - ICSP
  R1 = Resistor [tolerance=±5% resistance=100 package=THT]
  LED1 = LED - 5mm [color="Red (633nm)" package="5 mm [THT]"]
  R2 = Resistor [tolerance=±5% resistance=47 package=THT]
  C1 = Electrolytic Capacitor [capacitance=10µF package="1010 [SMD, electrolytic]"]

nets:
  N1: IR2.Data, IR3.Data, Part1.D5_PWM
  GND: IR2.GND, IR3.GND, Part1.GND, R2.Pin_0, C1.-
  N2: IR2.Vs, IR3.Vs, R1.Pin_1, C1.+
  N3: Part1.5V, R1.Pin_0
  N4: Part1.D2, LED1.anode
  N5: LED1.cathode, R2.Pin_1

custom parts:
  TSOP34838: The TSOP322.., TSOP348.., TSOP324.. and TSOP344.. series are miniaturized IR receiver modules for infrared remote control systems. A PIN diode and a preamplifier are assembled on lead frame, the epoxy package contains an IR filter. The demodulated output signal can be directly connected to a microprocessor for decoding. The TSOP324.., TSOP344.. series devices are optimized to suppress almost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
